// Logisim project coemips.circ as structural Verilog: 18 circuits, main circuit main
module main (
  output [15:0] out_1
);

  wire alunew_1_branch, and_1_out, clock_1_out, controlled_buffer_1_out, decoder_1_subop, decoder_1_unsigned,
       jr_1_jr, maincontrol_1_alusrc, maincontrol_1_branch, maincontrol_1_halt, maincontrol_1_jump,
       maincontrol_1_memread, maincontrol_1_memtoreg, maincontrol_1_memwrite, maincontrol_1_put,
       maincontrol_1_regwrite, multiplexer_2_out, multiplexer_4_out, r_i_load_store_1_iformat,
       r_i_load_store_1_loadstore, r_i_load_store_1_rformat, roricontrol_1_mux1, roricontrol_1_mux2,
       roricontrol_1_mux3, roricontrol_1_mux4;
  wire [2:0] decoder_1_rs, decoder_1_rt, maincontrol_1_aluop, multiplexer_3_out;
  wire [3:0] decoder_1_opcode, decoder_1_shamt, multiplexer_1_out;
  wire [7:0] adder_1_out, decoder_1_immediate, register_1_q;
  wire [15:0] alunew_1_result, bit_extender_1_out, bit_extender_2_out, bit_extender_3_out, multiplexer_5_out,
       multiplexer_6_out, multiplexer_7_out, multiplexer_8_out, multiplexer_10_out, ram_1_data,
       registefile_1_readdata1, registefile_1_readdata2, register_2_q, rom_1_data;

  Adder adder_1 (.a(register_1_q), .b(8'h1), .out(adder_1_out));  // open: cin, cout
  Register register_1 (.D(out_1[7:0]), .en(controlled_buffer_1_out), .Q(register_1_q), .clk(clock_1_out));  // open: clr
  Clock clock_1 (.out(clock_1_out));
  assign controlled_buffer_1_out = maincontrol_1_halt ? clock_1_out : 1'bz;  // Controlled_Buffer controlled_buffer_1
  LED Halt (.in(maincontrol_1_halt));
  ROM #(.dataWidth(16)) rom_1 (.addr(register_1_q), .data(rom_1_data));  // open: sel
  R_I_Load_Store r_i_load_store_1 (
    .in_1(rom_1_data), .Rformat(r_i_load_store_1_rformat), .Iformat(r_i_load_store_1_iformat),
    .LoadStore(r_i_load_store_1_loadstore));
  RorIcontrol roricontrol_1 (
    .R(r_i_load_store_1_rformat), .I(r_i_load_store_1_iformat), .LoadS(r_i_load_store_1_loadstore),
    .mux1(roricontrol_1_mux1), .mux2(roricontrol_1_mux2), .mux3(roricontrol_1_mux3), .mux4(roricontrol_1_mux4));
  Decoder decoder_1 (
    .in_1(rom_1_data), .immediate(decoder_1_immediate), .rt(decoder_1_rt), .rs(decoder_1_rs),
    .\unsigned (decoder_1_unsigned), .opcode(decoder_1_opcode), .Subop(decoder_1_subop),
    .shamt(decoder_1_shamt));
  Multiplexer #(.width(4), .enable("false")) multiplexer_1 (
    .in0(decoder_1_shamt), .in1(4'b0000), .out(multiplexer_1_out), .sel(roricontrol_1_mux3));
  jr jr_1 (
    .a(decoder_1_opcode[3]), .b(decoder_1_opcode[2]), .c(decoder_1_opcode[1]), .d(decoder_1_opcode[0]),
    .jr(jr_1_jr));
  MainControl maincontrol_1 (
    .Lower3(decoder_1_opcode[3]), .Lower2(decoder_1_opcode[2]), .Lower1(decoder_1_opcode[1]),
    .Lower0(decoder_1_opcode[0]), .Subop(multiplexer_2_out), .Branch(maincontrol_1_branch),
    .MemRead(maincontrol_1_memread), .MemToReg(maincontrol_1_memtoreg), .MemWrite(maincontrol_1_memwrite),
    .RegWrite(maincontrol_1_regwrite), .ALUSrc(maincontrol_1_alusrc), .ALUop2(maincontrol_1_aluop[2]),
    .ALUop1(maincontrol_1_aluop[1]), .ALUOp(maincontrol_1_aluop[0]), .put(maincontrol_1_put),
    .halt(maincontrol_1_halt), .jump(maincontrol_1_jump));
  Multiplexer #(.enable("false")) multiplexer_2 (
    .in0(decoder_1_subop), .in1(1'b0), .out(multiplexer_2_out), .sel(roricontrol_1_mux1));
  Multiplexer #(.width(3), .enable("false")) multiplexer_3 (
    .in0(decoder_1_rt), .in1(3'b000), .out(multiplexer_3_out), .sel(roricontrol_1_mux2));
  Multiplexer #(.enable("false")) multiplexer_4 (
    .in0(decoder_1_unsigned), .out(multiplexer_4_out), .sel(roricontrol_1_mux4));  // open: in1
  assign bit_extender_1_out = {{8{decoder_1_immediate[7]}}, decoder_1_immediate};  // Bit_Extender bit_extender_1
  assign bit_extender_2_out = {{8{1'b0}}, decoder_1_immediate};  // Bit_Extender bit_extender_2
  Multiplexer #(.width(16), .enable("false")) multiplexer_5 (
    .in0(bit_extender_1_out), .in1(bit_extender_2_out), .out(multiplexer_5_out), .sel(multiplexer_4_out));
  RegisteFile registefile_1 (
    .WriteData(multiplexer_10_out), .ReadData1(registefile_1_readdata1), .ReadRegister1(decoder_1_rs),
    .WriteEnable(maincontrol_1_regwrite), .ReadData2(registefile_1_readdata2),
    .ReadRegister2(multiplexer_3_out), .WriteRegister(decoder_1_rs), .clock(clock_1_out));
  assign bit_extender_3_out = {{8{1'b0}}, adder_1_out};  // Bit_Extender bit_extender_3
  Multiplexer #(.width(16), .enable("false")) multiplexer_6 (
    .in0(registefile_1_readdata2), .in1(multiplexer_5_out), .out(multiplexer_6_out),
    .sel(maincontrol_1_alusrc));
  and and_1 (and_1_out, maincontrol_1_branch, alunew_1_branch);
  ALUnew alunew_1 (
    .A(registefile_1_readdata1), .B(multiplexer_6_out), .shamt(multiplexer_1_out),
    .opcode(maincontrol_1_aluop), .Branch(alunew_1_branch), .result(alunew_1_result));
  Register #(.width(16)) register_2 (
    .D(registefile_1_readdata1), .en(maincontrol_1_put), .Q(register_2_q), .clk(clock_1_out));  // open: clr
  Multiplexer #(.width(16), .enable("false")) multiplexer_7 (
    .in0(bit_extender_3_out), .in1(multiplexer_5_out), .out(multiplexer_7_out), .sel(and_1_out));
  Multiplexer #(.width(16), .enable("false")) multiplexer_8 (
    .in0(multiplexer_7_out), .in1(multiplexer_5_out), .out(multiplexer_8_out), .sel(maincontrol_1_jump));
  Hex_Digit_Display hex_digit_display_1 (.value(register_2_q[15:12]));  // open: dp
  Multiplexer #(.width(16), .enable("false")) multiplexer_9 (
    .in0(multiplexer_8_out), .in1(registefile_1_readdata1), .out(out_1), .sel(jr_1_jr));
  Hex_Digit_Display hex_digit_display_2 (.value(register_2_q[11:8]));  // open: dp
  Hex_Digit_Display hex_digit_display_3 (.value(register_2_q[3:0]));  // open: dp
  Hex_Digit_Display hex_digit_display_4 (.value(register_2_q[7:4]));  // open: dp
  RAM #(.dataWidth(16), .bus("separate")) ram_1 (
    .addr(alunew_1_result[7:0]), .din(registefile_1_readdata2), .data(ram_1_data),
    .str(maincontrol_1_memwrite), .clk(clock_1_out), .ld(maincontrol_1_memread));  // open: sel, clr
  Multiplexer #(.width(16), .enable("false")) multiplexer_10 (
    .in0(ram_1_data), .in1(alunew_1_result), .out(multiplexer_10_out), .sel(maincontrol_1_memtoreg));

  // Notes on the sheet:
  //   contents of rom_1 (hex, n*v repeats v):
  //   1 f000 1001 241 200 12f0 b201 10ff 481 1503 5008 f000 14ff a40a 1 1108 5018 901 190f 5818 481 1504
  //   f000 6c1 600 3701 5609 30c0 3000 5809 14ff 8421 8e16 7000
endmodule

module ALU (
  input  Binvert,
  input  Ainvert,
  input  Cin,
  input  [1:0] OP,
  input  A,
  input  B,
  input  less,
  output Result,
  output Cout
);

  wire adder_1_out, and_1_out, multiplexer_1_out, multiplexer_2_out, not_1_out, not_2_out, or_1_out;

  not not_1 (not_1_out, A);
  not not_2 (not_2_out, B);
  Multiplexer #(.enable("false")) multiplexer_1 (.in0(A), .in1(not_1_out), .out(multiplexer_1_out), .sel(Ainvert));
  Multiplexer #(.enable("false")) multiplexer_2 (.in0(B), .in1(not_2_out), .out(multiplexer_2_out), .sel(Binvert));
  and and_1 (and_1_out, multiplexer_1_out, multiplexer_2_out);
  or or_1 (or_1_out, multiplexer_1_out, multiplexer_2_out);
  Adder #(.width(1)) adder_1 (.a(multiplexer_1_out), .b(multiplexer_2_out), .out(adder_1_out), .cin(Cin), .cout(Cout));
  Multiplexer #(.select(2), .enable("false")) multiplexer_3 (
    .in0(and_1_out), .in1(or_1_out), .in2(adder_1_out), .in3(less), .out(Result), .sel(OP));
endmodule

module RegisteFile (
  input  [15:0] WriteData,
  input  [2:0] ReadRegister1,
  input  [2:0] ReadRegister2,
  input  WriteEnable,
  input  [2:0] WriteRegister,
  input  clock,
  output [15:0] ReadData1,
  output [15:0] ReadData2
);

  wire demultiplexer_1_out0, demultiplexer_1_out1, demultiplexer_1_out2, demultiplexer_1_out3,
       demultiplexer_1_out4, demultiplexer_1_out5, demultiplexer_1_out6, demultiplexer_1_out7;
  wire [15:0] Reg_0_q, Reg_1_q, Reg_2_q, Reg_3_q, Reg_4_q, Reg_5_q, Reg_6_q, Reg_7_q;

  Demultiplexer #(.select(3), .enable("false")) demultiplexer_1 (
    .out0(demultiplexer_1_out0), .out1(demultiplexer_1_out1), .out2(demultiplexer_1_out2),
    .out3(demultiplexer_1_out3), .out4(demultiplexer_1_out4), .out5(demultiplexer_1_out5),
    .out6(demultiplexer_1_out6), .out7(demultiplexer_1_out7), .in(WriteEnable), .sel(WriteRegister));
  Register #(.width(16)) Reg_0 (.D(WriteData), .en(demultiplexer_1_out0), .Q(Reg_0_q), .clk(clock));  // open: clr
  Register #(.width(16)) Reg_1 (.D(WriteData), .en(demultiplexer_1_out1), .Q(Reg_1_q), .clk(clock));  // open: clr
  Register #(.width(16)) Reg_2 (.D(WriteData), .en(demultiplexer_1_out2), .Q(Reg_2_q), .clk(clock));  // open: clr
  Register #(.width(16)) Reg_3 (.D(WriteData), .en(demultiplexer_1_out3), .Q(Reg_3_q), .clk(clock));  // open: clr
  Register #(.width(16)) Reg_4 (.D(WriteData), .en(demultiplexer_1_out4), .Q(Reg_4_q), .clk(clock));  // open: clr
  Register #(.width(16)) Reg_5 (.D(WriteData), .en(demultiplexer_1_out5), .Q(Reg_5_q), .clk(clock));  // open: clr
  Register #(.width(16)) Reg_6 (.D(WriteData), .en(demultiplexer_1_out6), .Q(Reg_6_q), .clk(clock));  // open: clr
  Register #(.width(16)) Reg_7 (.D(WriteData), .en(demultiplexer_1_out7), .Q(Reg_7_q), .clk(clock));  // open: clr
  Multiplexer #(.select(3), .width(16), .enable("false")) multiplexer_1 (
    .in0(Reg_0_q), .in1(Reg_1_q), .in2(Reg_2_q), .in3(Reg_3_q), .in4(Reg_4_q), .in5(Reg_5_q), .in6(Reg_6_q),
    .in7(Reg_7_q), .out(ReadData1), .sel(ReadRegister1));
  Multiplexer #(.select(3), .width(16), .enable("false")) multiplexer_2 (
    .in0(Reg_0_q), .in1(Reg_1_q), .in2(Reg_2_q), .in3(Reg_3_q), .in4(Reg_4_q), .in5(Reg_5_q), .in6(Reg_6_q),
    .in7(Reg_7_q), .out(ReadData2), .sel(ReadRegister2));
endmodule

module ALUcontrol (
  input  SupOP,
  output Binvert,
  output Cin
);


  assign Binvert = SupOP;
  assign Cin = SupOP;
endmodule

module RorI (
  input  [15:0] in_1,
  output Rformat,
  output Iformat,
  output Load_Store
);

  wire and_2_out, and_3_out, and_4_out, and_5_out, and_6_out, and_7_out, and_8_out, and_9_out, not_1_out,
       not_2_out, not_3_out, not_4_out, not_5_out, not_6_out, not_7_out, not_8_out, not_9_out, not_10_out,
       not_11_out, not_12_out, not_13_out, not_14_out;

  not not_1 (not_1_out, in_1[13]);
  not not_2 (not_2_out, in_1[14]);
  not not_3 (not_3_out, in_1[12]);
  not not_4 (not_4_out, in_1[13]);
  not not_5 (not_5_out, in_1[15]);
  not not_6 (not_6_out, in_1[12]);
  not not_7 (not_7_out, in_1[14]);
  not not_8 (not_8_out, in_1[15]);
  not not_9 (not_9_out, in_1[12]);
  not not_10 (not_10_out, in_1[14]);
  not not_11 (not_11_out, in_1[13]);
  not not_12 (not_12_out, in_1[14]);
  not not_13 (not_13_out, in_1[15]);
  not not_14 (not_14_out, in_1[15]);
  and and_1 (Load_Store, in_1[12], not_1_out, not_2_out, in_1[15]);
  and and_2 (and_2_out, not_3_out, not_4_out, not_5_out);
  and and_3 (and_3_out, not_6_out, not_7_out, not_8_out);
  and and_4 (and_4_out, not_9_out, in_1[14], in_1[15]);
  and and_5 (and_5_out, in_1[13], not_10_out, in_1[15]);
  and and_6 (and_6_out, not_11_out, not_12_out, in_1[15]);
  and and_7 (and_7_out, in_1[13], in_1[14], not_13_out);
  and and_8 (and_8_out, in_1[12], not_14_out);
  and and_9 (and_9_out, in_1[12], in_1[14]);
  or or_1 (Rformat, and_2_out, and_3_out, and_4_out, and_5_out);
  or or_2 (Iformat, and_6_out, and_7_out, and_8_out, and_9_out);
endmodule

// D2
module RorIcontrol (
  input  R,
  input  I,
  input  LoadS,
  output mux1,
  output mux2,
  output mux3,
  output mux4
);

  wire and_1_out, not_3_out, not_4_out;

  not not_1 (mux1, R);
  not not_2 (mux3, R);
  not not_3 (not_3_out, I);
  not not_4 (not_4_out, LoadS);
  and and_1 (and_1_out, not_3_out, not_4_out);
  or or_1 (mux4, and_1_out, R);

  assign mux2 = I;
endmodule

module Overflow (
  input  a31,
  input  b31,
  input  Binv,
  input  Cin,
  input  op,
  input  op1,
  input  r31,
  output overflow
);

  wire and_1_out, and_2_out, and_3_out, and_4_out, not_1_out, not_2_out, not_3_out, not_4_out, not_5_out,
       not_6_out, not_7_out, not_8_out, not_9_out, not_10_out, not_11_out, not_12_out, not_13_out, not_14_out;

  not not_1 (not_1_out, a31);
  not not_2 (not_2_out, b31);
  not not_3 (not_3_out, Binv);
  not not_4 (not_4_out, Cin);
  not not_5 (not_5_out, op1);
  not not_6 (not_6_out, a31);
  not not_7 (not_7_out, op1);
  not not_8 (not_8_out, b31);
  not not_9 (not_9_out, op1);
  not not_10 (not_10_out, r31);
  not not_11 (not_11_out, Binv);
  not not_12 (not_12_out, Cin);
  not not_13 (not_13_out, op1);
  not not_14 (not_14_out, r31);
  and and_1 (and_1_out, not_1_out, not_2_out, not_3_out, not_4_out, op, not_5_out, r31);
  and and_2 (and_2_out, not_6_out, b31, Binv, Cin, op, not_7_out, r31);
  and and_3 (and_3_out, a31, not_8_out, Binv, Cin, op, not_9_out, not_10_out);
  and and_4 (and_4_out, a31, b31, not_11_out, not_12_out, op, not_13_out, not_14_out);
  or or_1 (overflow, and_1_out, and_2_out, and_3_out, and_4_out);
endmodule

module Check (
  input  [15:0] in_1,
  output [7:0] out_2,
  output [15:0] out_3,
  output [15:0] out_4,
  output [2:0] out_5,
  output [2:0] out_6,
  output [15:0] out_7,
  output [15:0] out_8
);

  wire alunew_1_branch, and_1_out, clock_1_out, controlled_buffer_1_out, decoder_1_subop, decoder_1_unsigned,
       rori_1_p4, rori_1_p5, rori_1_p6, rori_1_p7, rori_1_p8, rori_1_p9, undriven, undriven_2;
  wire [2:0] undriven_3;
  wire [3:0] decoder_1_opcode, decoder_1_shamt;
  wire [7:0] adder_1_out, decoder_1_immediate, register_1_q;
  wire [15:0] alunew_2_result, bit_extender_1_out, bit_extender_2_out, bit_extender_3_out, multiplexer_1_out,
       multiplexer_3_out, ram_1_data, registefile_1_p4, registefile_1_p8, register_2_q, rom_1_data;

  Adder adder_1 (.a(register_1_q), .b(8'h1), .out(adder_1_out));  // open: cin, cout
  Register register_1 (
    .D(multiplexer_3_out[7:0]), .en(controlled_buffer_1_out), .Q(register_1_q), .clk(clock_1_out));  // open: clr
  Clock clock_1 (.out(clock_1_out));
  assign controlled_buffer_1_out = undriven ? clock_1_out : 1'bz;  // Controlled_Buffer controlled_buffer_1
  Decoder decoder_1 (
    .in_1(in_1), .immediate(decoder_1_immediate), .rt(out_6), .rs(out_5), .\unsigned (decoder_1_unsigned),
    .opcode(decoder_1_opcode), .Subop(decoder_1_subop), .shamt(decoder_1_shamt));
  ROM #(.dataWidth(16)) rom_1 (.addr(register_1_q), .data(rom_1_data));  // open: sel
  // RorI rori_1: pin names not known; wires that end beside it: decoder_1_opcode[3], decoder_1_opcode[2], decoder_1_opcode[1], rori_1_p4, rori_1_p5, rori_1_p6, rori_1_p7, rori_1_p8, rori_1_p9
  assign bit_extender_1_out = {{8{decoder_1_immediate[7]}}, decoder_1_immediate};  // Bit_Extender bit_extender_1
  assign bit_extender_2_out = {{8{1'b0}}, decoder_1_immediate};  // Bit_Extender bit_extender_2
  Multiplexer #(.width(16), .enable("false")) multiplexer_1 (
    .in0(bit_extender_1_out), .in1(bit_extender_2_out), .out(multiplexer_1_out), .sel(decoder_1_unsigned));
  LED halt (.in(undriven));
  // RegisteFile registefile_1: pin names not known; wires that end beside it: out_5, out_6, out_5, registefile_1_p4, clock_1_out, rori_1_p8, out_3, registefile_1_p8
  Multiplexer #(.width(16), .enable("false")) multiplexer_2 (
    .in0(registefile_1_p8), .in1(multiplexer_1_out), .out(out_4), .sel(rori_1_p9));
  assign bit_extender_3_out = {{8{1'b0}}, adder_1_out};  // Bit_Extender bit_extender_3
  ALUnew alunew_1 (
    .A(out_3), .B(out_4), .shamt(decoder_1_shamt), .opcode(undriven_3), .Branch(alunew_1_branch),
    .result({out_7[15:8], out_2}));
  Register #(.width(16)) register_2 (.D(out_3), .en(undriven_2), .Q(register_2_q), .clk(clock_1_out));  // open: clr
  ALUnew alunew_2 (
    .A(bit_extender_3_out), .B({out_7[15:8], out_2}), .shamt(4'b0010), .opcode(undriven_3),
    .result(alunew_2_result));  // open: Branch
  and and_1 (and_1_out, rori_1_p4, alunew_1_branch);
  Hex_Digit_Display hex_digit_display_1 (.value(register_2_q[3:0]));  // open: dp
  Hex_Digit_Display hex_digit_display_2 (.value(register_2_q[7:4]));  // open: dp
  Multiplexer #(.width(16), .enable("false")) multiplexer_3 (
    .in0(bit_extender_3_out), .in1(alunew_2_result), .out(multiplexer_3_out), .sel(and_1_out));
  Hex_Digit_Display hex_digit_display_3 (.value(register_2_q[11:8]));  // open: dp
  Hex_Digit_Display hex_digit_display_4 (.value(register_2_q[15:12]));  // open: dp
  RAM #(.dataWidth(16), .bus("separate")) ram_1 (
    .addr(out_2), .din(out_4), .data(ram_1_data), .str(rori_1_p7), .ld(rori_1_p5));  // open: sel, clk, clr
  Multiplexer #(.width(16), .enable("false")) multiplexer_4 (
    .in0(ram_1_data), .in1({out_7[15:8], out_2}), .out(registefile_1_p4), .sel(rori_1_p6));

  assign out_7[7:0] = out_2;
  assign out_8 = out_4;

  // Notes on the sheet:
  //   contents of rom_1 (hex, n*v repeats v):
  //   1 f000 1001 241 200 12f0 b201 10ff 481 1503 5008 f000 14ff a40a 1 1108 5018 901 190f 5818 481 1504
  //   f000 6c1 600 3701 5609 30c0 3000 5809 14ff 8421 8e16 7000
endmodule

module check2 (
  input  [15:0] WriteData,
  input  [2:0] ReadRegister1,
  input  [2:0] ReadRegister2,
  input  WriteEnable,
  input  [2:0] WriteRegister,
  output [15:0] ReadData1,
  output [15:0] ReadData2
);

  wire clock_1_out, decoder_1_out0, decoder_1_out1, decoder_1_out2, decoder_1_out3, decoder_1_out4,
       decoder_1_out5, decoder_1_out6, decoder_1_out7, not_2_out, not_3_out, not_4_out, not_5_out, not_6_out,
       not_7_out, not_8_out;
  wire [15:0] Reg_0_q, Reg_1_q, Reg_2_q, Reg_3_q, Reg_4_q, Reg_5_q, Reg_6_q, Reg_7_q;

  Decoder_part #(.select(3), .disabled(0)) decoder_1 (
    .out0(decoder_1_out0), .out1(decoder_1_out1), .out2(decoder_1_out2), .out3(decoder_1_out3),
    .out4(decoder_1_out4), .out5(decoder_1_out5), .out6(decoder_1_out6), .out7(decoder_1_out7),
    .sel(WriteRegister), .en(WriteEnable));
  not not_1 (WriteEnable, decoder_1_out5);
  not not_2 (not_2_out, decoder_1_out6);
  not not_3 (not_3_out, decoder_1_out7);
  not not_4 (not_4_out, decoder_1_out3);
  not not_5 (not_5_out, decoder_1_out4);
  not not_6 (not_6_out, decoder_1_out0);
  Clock clock_1 (.out(clock_1_out));
  not not_7 (not_7_out, decoder_1_out1);
  not not_8 (not_8_out, decoder_1_out2);
  Register #(.width(16)) Reg_0 (.D(WriteData), .en(WriteEnable), .Q(Reg_0_q), .clk(clock_1_out), .clr(not_6_out));
  Register #(.width(16)) Reg_1 (.D(WriteData), .Q(Reg_1_q), .clk(clock_1_out), .clr(not_7_out));  // open: en
  Register #(.width(16)) Reg_2 (.D(WriteData), .Q(Reg_2_q), .clk(clock_1_out), .clr(not_8_out));  // open: en
  Register #(.width(16)) Reg_3 (.D(WriteData), .Q(Reg_3_q), .clk(clock_1_out), .clr(not_4_out));  // open: en
  Register #(.width(16)) Reg_4 (.D(WriteData), .Q(Reg_4_q), .clk(clock_1_out), .clr(not_5_out));  // open: en
  Register #(.width(16)) Reg_5 (.D(WriteData), .Q(Reg_5_q), .clk(clock_1_out), .clr(WriteEnable));  // open: en
  Register #(.width(16)) Reg_6 (.D(WriteData), .Q(Reg_6_q), .clk(clock_1_out), .clr(not_2_out));  // open: en
  Register #(.width(16)) Reg_7 (.D(WriteData), .Q(Reg_7_q), .clk(clock_1_out), .clr(not_3_out));  // open: en
  Multiplexer #(.select(3), .width(16), .enable("false")) multiplexer_1 (
    .in0(Reg_0_q), .in1(Reg_1_q), .in2(Reg_2_q), .in3(Reg_3_q), .in4(Reg_4_q), .in5(Reg_5_q), .in6(Reg_6_q),
    .in7(Reg_7_q), .out(ReadData1), .sel(ReadRegister1));
  Multiplexer #(.select(3), .width(16), .enable("false")) multiplexer_2 (
    .in0(Reg_0_q), .in1(Reg_1_q), .in2(Reg_2_q), .in3(Reg_3_q), .in4(Reg_4_q), .in5(Reg_5_q), .in6(Reg_6_q),
    .in7(Reg_7_q), .out(ReadData2), .sel(ReadRegister2));
endmodule

// Deocder
module Decoder (
  input  [15:0] in_1,
  output Subop,
  output [7:0] immediate,
  output [3:0] shamt,
  output [2:0] rt,
  output [2:0] rs,
  output \unsigned ,
  output [3:0] opcode
);


  assign immediate = in_1[7:0];
  assign opcode = in_1[15:12];
  assign rs = in_1[11:9];
  assign rt = in_1[8:6];
  assign shamt = in_1[4:1];
  assign Subop = in_1[0];
  assign \unsigned  = in_1[8];
endmodule

// ALU
module ALUnew (
  input  [15:0] A,
  input  [15:0] B,
  input  [2:0] opcode,
  input  [3:0] shamt,
  output Branch,
  output [15:0] result
);

  wire comparator_1_eq, comparator_1_gt, comparator_1_lt, not_1_out;
  wire [15:0] adder_1_out, and_1_out, nor_1_out, shifter_1_out, shifter_2_out, shifter_3_out, shifter_4_out,
       subtractor_1_out;

  Adder #(.width(16)) adder_1 (.a(A), .b(B), .out(adder_1_out));  // open: cin, cout
  Subtractor #(.width(16)) subtractor_1 (.a(A), .b(B), .out(subtractor_1_out));  // open: bin, bout
  assign and_1_out = A & B;  // AND_Gate and_1, 16 bits wide
  Shifter #(.width(16)) shifter_1 (.in(A), .\dist (shamt), .out(shifter_1_out));
  Shifter #(.width(16), .shift("lr")) shifter_2 (.in(A), .\dist (shamt), .out(shifter_2_out));
  Shifter #(.width(16)) shifter_3 (.in(A), .\dist (B[3:0]), .out(shifter_3_out));
  Shifter #(.width(16), .shift("lr")) shifter_4 (.in(A), .\dist (B[3:0]), .out(shifter_4_out));
  assign nor_1_out = ~(A | B);  // NOR_Gate nor_1, 16 bits wide
  Multiplexer #(.select(3), .width(16), .enable("false")) multiplexer_1 (
    .in0(adder_1_out), .in1(subtractor_1_out), .in2(nor_1_out), .in3(and_1_out), .in4(shifter_1_out),
    .in5(shifter_2_out), .in6(shifter_3_out), .in7(shifter_4_out), .out(result), .sel(opcode));
  Comparator #(.width(16)) comparator_1 (
    .a(A), .b({16{1'b0}}), .gt(comparator_1_gt), .eq(comparator_1_eq), .lt(comparator_1_lt));
  not not_1 (not_1_out, comparator_1_eq);
  Multiplexer #(.select(2)) multiplexer_2 (
    .in0(comparator_1_eq), .in1(not_1_out), .in2(comparator_1_gt), .in3(comparator_1_lt), .out(Branch),
    .sel(opcode[1:0]));  // open: en

  // Notes on the sheet:
  //   srl
  //   sll
  //   srlv
  //   sllv
endmodule

module Rcontrol (
  input  [15:0] \input ,
  output subOP,
  output [3:0] shamt,
  output [2:0] Rt,
  output \unsigned ,
  output [2:0] Rs,
  output [3:0] opcode
);


  assign opcode = \input [15:12];
  assign Rs = \input [11:9];
  assign Rt = \input [8:6];
  assign shamt = \input [4:1];
  assign subOP = \input [0];
  assign \unsigned  = \input [8];
endmodule

module PC (
  input  [15:0] in_1,
  input  _0,
  input  in_3,
  input  in_4,
  input  in_5,
  input  [7:0] D,
  input  _3,
  input  [7:0] D_2,
  input  Halt,
  input  Halt_2,
  output [7:0] Cin,
  output Rformat,
  output [7:0] Q,
  output Iformat,
  output [7:0] Cin_2
);

  wire and_1_out, and_2_out, and_3_out, and_4_out, and_5_out, and_6_out, and_7_out, clock_1_out, clock_2_out,
       controlled_buffer_1_out, not_1_out, not_2_out, not_3_out, not_4_out, not_5_out, not_6_out, not_7_out,
       undriven_2;
  wire [2:0] undriven_4;
  wire [7:0] undriven;
  wire [15:0] alunew_1_result, bit_extender_1_out, multiplexer_1_out, shifter_1_out, undriven_3;

  Adder adder_1 (.a(Q), .b(8'h1), .out(D));  // open: cin, cout
  Register register_1 (.D(D), .en(controlled_buffer_1_out), .Q(Q), .clk(clock_1_out));  // open: clr
  Clock clock_1 (.out(clock_1_out));
  assign controlled_buffer_1_out = Halt ? clock_1_out : 1'bz;  // Controlled_Buffer controlled_buffer_1
  Register register_2 (.D(D_2), .en(Halt_2), .Q(Cin_2), .clk(clock_2_out));  // open: clr
  Clock clock_2 (.out(clock_2_out));
  not not_1 (not_1_out, in_1[15]);
  not not_2 (not_2_out, in_1[12]);
  not not_3 (not_3_out, in_1[15]);
  not not_4 (not_4_out, in_1[13]);
  not not_5 (not_5_out, in_1[14]);
  not not_6 (not_6_out, in_1[13]);
  not not_7 (not_7_out, in_1[12]);
  and and_1 (and_1_out, not_1_out, not_2_out);
  or or_1 (Rformat, and_1_out, and_2_out, and_3_out);
  and and_2 (and_2_out, not_3_out, in_1[13]);
  and and_3 (and_3_out, in_1[14], not_4_out, in_1[12]);
  and and_4 (and_4_out, not_5_out, not_6_out, in_1[12]);
  and and_5 (and_5_out, in_1[15], not_7_out);
  or or_2 (Iformat, and_4_out, and_5_out, and_6_out);
  and and_6 (and_6_out, in_1[15], in_1[13]);
  assign bit_extender_1_out = {{8{1'b0}}, undriven};  // Bit_Extender bit_extender_1
  Shifter #(.width(16)) shifter_1 (.in(undriven_3), .\dist (4'b0010), .out(shifter_1_out));
  buf and_7 (and_7_out, undriven_2);  // AND_Gate
  ALUnew alunew_1 (
    .A(bit_extender_1_out), .B(shifter_1_out), .opcode(undriven_4), .result(alunew_1_result));  // open: shamt, Branch
  Multiplexer #(.width(16), .enable("false")) multiplexer_1 (
    .in0(bit_extender_1_out), .in1(alunew_1_result), .out(multiplexer_1_out), .sel(and_7_out));

  assign Cin = D;
endmodule

module put (
  input  [15:0] in_1,
  input  [7:0] in_2,
  input  [7:0] in_3,
  input  in_4,
  input  in_5,
  input  [2:0] in_6,
  input  [2:0] in_7,
  input  in_8,
  input  [2:0] in_9,
  input  [15:0] in_10,
  output [7:0] out_11,
  output [15:0] out_12
);

  wire clock_1_out, clock_2_out, undriven;
  wire [3:0] register_2_q, register_2_q_2, register_2_q_3, register_2_q_4;
  wire [7:0] ram_1_data;

  RegisteFile registefile_1 (
    .WriteData(in_10), .ReadData1(out_12), .ReadRegister1(in_6), .WriteEnable(in_5), .ReadRegister2(in_7),
    .WriteRegister(in_9), .clock(clock_1_out));  // open: ReadData2
  Clock clock_1 (.out(clock_1_out));
  RAM #(.bus("separate")) ram_1 (
    .addr(in_2), .din(in_3), .data(ram_1_data), .str(in_4), .clk(clock_2_out), .ld(undriven));  // open: sel, clr
  Clock clock_2 (.out(clock_2_out));
  Register register_1 (.D(ram_1_data), .Q(out_11), .clk(clock_2_out));  // open: en, clr
  Register #(.width(16)) register_2 (
    .D(out_12), .en(in_8), .Q({register_2_q_4, register_2_q_3, register_2_q_2, register_2_q}),
    .clk(clock_1_out));  // open: clr
  Hex_Digit_Display hex_digit_display_1 (.value(ram_1_data[7:4]));  // open: dp
  Hex_Digit_Display hex_digit_display_2 (.value(register_2_q_3));  // open: dp
  Hex_Digit_Display hex_digit_display_3 (.value(register_2_q_4));  // open: dp
  Hex_Digit_Display hex_digit_display_4 (.value(ram_1_data[3:0]));  // open: dp
  Hex_Digit_Display hex_digit_display_5 (.value(register_2_q_2));  // open: dp
  Hex_Digit_Display hex_digit_display_6 (.value(register_2_q));  // open: dp
endmodule

module Iformat (
  input  [15:0] \input ,
  output [7:0] Imm,
  output [2:0] Rs,
  output [3:0] OPcode
);


  assign Imm = \input [7:0];
  assign OPcode = \input [15:12];
  assign Rs = \input [11:9];
endmodule

// control
module MainControl (
  input  Lower3,
  input  Lower2,
  input  Lower1,
  input  Lower0,
  input  Subop,
  output Branch,
  output MemRead,
  output MemToReg,
  output MemWrite,
  output RegWrite,
  output ALUSrc,
  output ALUop2,
  output ALUop1,
  output ALUOp,
  output put,
  output halt,
  output jump
);

  wire and_3_out, and_4_out, and_5_out, and_6_out, and_7_out, and_8_out, and_9_out, and_10_out, and_11_out,
       and_12_out, and_13_out, and_14_out, and_15_out, and_16_out, and_17_out, and_18_out, and_19_out,
       and_20_out, and_21_out, and_22_out, and_23_out, and_25_out, and_26_out, and_27_out, and_28_out,
       and_29_out, and_30_out, and_31_out, and_32_out, and_33_out, and_35_out, and_36_out, not_1_out,
       not_2_out, not_3_out, not_4_out, not_5_out, not_6_out, not_7_out, not_8_out, not_9_out, not_10_out,
       not_11_out, not_12_out, not_13_out, not_14_out, not_15_out, not_16_out, not_17_out, not_18_out,
       not_19_out, not_20_out, not_21_out, not_22_out, not_23_out, not_24_out, not_25_out, not_26_out,
       not_27_out, not_28_out, not_29_out, not_30_out, not_31_out, not_32_out, not_33_out, not_34_out,
       not_35_out, not_36_out, not_37_out, not_38_out, not_39_out, not_40_out, not_41_out, not_42_out,
       not_43_out, not_44_out, not_45_out, not_46_out, not_47_out, not_48_out, not_49_out, not_50_out,
       not_51_out, not_52_out, not_53_out, not_54_out, not_55_out, not_56_out, not_57_out, not_58_out,
       not_59_out, not_60_out, not_61_out, not_62_out, not_63_out, not_64_out, not_65_out;

  not not_1 (not_1_out, Lower2);
  not not_2 (not_2_out, Lower3);
  not not_3 (not_3_out, Lower1);
  not not_4 (not_4_out, Lower3);
  not not_5 (not_5_out, Lower1);
  not not_6 (not_6_out, Lower3);
  not not_7 (not_7_out, Lower0);
  not not_8 (not_8_out, Subop);
  not not_9 (not_9_out, Lower1);
  not not_10 (not_10_out, Lower3);
  not not_11 (not_11_out, Lower2);
  not not_12 (not_12_out, Lower1);
  not not_13 (not_13_out, Lower3);
  not not_14 (not_14_out, Lower2);
  not not_15 (not_15_out, Lower3);
  not not_16 (not_16_out, Lower0);
  not not_17 (not_17_out, Lower3);
  not not_18 (not_18_out, Lower2);
  not not_19 (not_19_out, Lower1);
  not not_20 (not_20_out, Lower3);
  not not_21 (not_21_out, Lower2);
  not not_22 (not_22_out, Lower0);
  not not_23 (not_23_out, Subop);
  not not_24 (not_24_out, Lower3);
  not not_25 (not_25_out, Lower1);
  not not_26 (not_26_out, Lower1);
  not not_27 (not_27_out, Lower0);
  not not_28 (not_28_out, Lower3);
  not not_29 (not_29_out, Lower0);
  not not_30 (not_30_out, Lower3);
  not not_31 (not_31_out, Lower2);
  not not_32 (not_32_out, Lower3);
  not not_33 (not_33_out, Subop);
  not not_34 (not_34_out, Lower3);
  not not_35 (not_35_out, Lower1);
  not not_36 (not_36_out, Lower0);
  not not_37 (not_37_out, Lower3);
  not not_38 (not_38_out, Lower2);
  not not_39 (not_39_out, Lower1);
  not not_40 (not_40_out, Lower3);
  not not_41 (not_41_out, Lower1);
  not not_42 (not_42_out, Subop);
  not not_43 (not_43_out, Lower3);
  not not_44 (not_44_out, Lower0);
  not not_45 (not_45_out, Lower1);
  not not_46 (not_46_out, Lower0);
  not not_47 (not_47_out, Subop);
  not not_48 (not_48_out, Lower3);
  not not_49 (not_49_out, Lower1);
  not not_50 (not_50_out, Lower2);
  not not_51 (not_51_out, Lower1);
  not not_52 (not_52_out, Lower0);
  not not_53 (not_53_out, Lower1);
  not not_54 (not_54_out, Lower0);
  not not_55 (not_55_out, Lower3);
  not not_56 (not_56_out, Lower1);
  not not_57 (not_57_out, Lower0);
  not not_58 (not_58_out, Lower2);
  not not_59 (not_59_out, Lower3);
  not not_60 (not_60_out, Lower1);
  not not_61 (not_61_out, Lower2);
  not not_62 (not_62_out, Lower1);
  and and_1 (put, Lower3, Lower2, Lower1, Lower0);
  not not_63 (not_63_out, Lower3);
  not not_64 (not_64_out, Lower1);
  not not_65 (not_65_out, Lower0);
  and and_2 (Branch, Lower3, not_1_out);
  and and_3 (and_3_out, not_2_out, not_3_out, Lower0);
  and and_4 (and_4_out, not_4_out, Lower2, not_5_out);
  and and_5 (and_5_out, not_6_out, Lower2, not_7_out, not_8_out);
  and and_6 (and_6_out, Lower2, not_9_out, Lower0);
  and and_7 (and_7_out, not_10_out, not_11_out, not_12_out);
  and and_8 (and_8_out, not_13_out, not_14_out, Lower0);
  and and_9 (and_9_out, not_15_out, Lower2, Lower1, not_16_out);
  and and_10 (and_10_out, not_17_out, not_18_out, not_19_out);
  and and_11 (and_11_out, not_20_out, not_21_out, not_22_out, not_23_out);
  and and_12 (and_12_out, not_24_out, not_25_out, Subop);
  and and_13 (and_13_out, Lower2, not_26_out, not_27_out);
  and and_14 (and_14_out, not_28_out, Lower2, not_29_out, Subop);
  and and_15 (and_15_out, not_30_out, not_31_out);
  and and_16 (and_16_out, not_32_out, not_33_out);
  and and_17 (and_17_out, not_34_out, Lower0);
  and and_18 (and_18_out, Lower2, not_35_out);
  and and_19 (and_19_out, Lower3, Lower2, not_36_out);
  and and_20 (and_20_out, not_37_out, not_38_out, not_39_out, Lower0);
  and and_21 (and_21_out, not_40_out, not_41_out, Lower0, not_42_out);
  and and_22 (and_22_out, not_43_out, Lower2, Lower1, not_44_out);
  and and_23 (and_23_out, Lower3, Lower2, not_45_out, not_46_out, not_47_out);
  and and_24 (ALUop2, not_48_out, Lower2, not_49_out);
  and and_25 (and_25_out, not_50_out, Lower1);
  and and_26 (and_26_out, Lower2, not_51_out, not_52_out);
  and and_27 (and_27_out, Lower3, Lower2, not_53_out);
  and and_28 (and_28_out, Lower3, Lower2, not_54_out);
  and and_29 (and_29_out, not_55_out, not_56_out, not_57_out, Subop);
  and and_30 (and_30_out, not_58_out, Lower1, Lower0, Subop);
  and and_31 (and_31_out, not_59_out, Lower2, not_60_out, Subop);
  and and_32 (and_32_out, Lower3, not_61_out, Lower0);
  and and_33 (and_33_out, Lower3, not_62_out, Lower0);
  and and_34 (halt, not_63_out, Lower2, Lower1, Lower0);
  and and_35 (and_35_out, Lower3, Lower2, not_64_out);
  and and_36 (and_36_out, Lower3, Lower2, not_65_out);
  or or_1 (MemRead, and_3_out, and_4_out, and_5_out, and_6_out);
  or or_2 (MemToReg, and_7_out, and_8_out, and_9_out);
  or or_3 (MemWrite, and_10_out, and_11_out, and_12_out, and_13_out, and_14_out);
  or or_4 (RegWrite, and_15_out, and_16_out, and_17_out, and_18_out, and_19_out);
  or or_5 (ALUSrc, and_20_out, and_21_out, and_22_out, and_23_out);
  or or_6 (ALUop1, and_25_out, and_26_out, and_27_out, and_28_out);
  or or_7 (ALUOp, and_29_out, and_30_out, and_31_out, and_32_out, and_33_out);
  or or_8 (jump, and_35_out, and_36_out);
endmodule

// D1
module R_I_Load_Store (
  input  [15:0] in_1,
  output Rformat,
  output Iformat,
  output LoadStore
);

  wire and_1_out, and_2_out, and_3_out, and_4_out, and_5_out, and_6_out, not_1_out, not_2_out, not_3_out,
       not_4_out, not_5_out, not_6_out, not_7_out, not_8_out, not_9_out, not_10_out;

  not not_1 (not_1_out, in_1[15]);
  not not_2 (not_2_out, in_1[13]);
  not not_3 (not_3_out, in_1[12]);
  not not_4 (not_4_out, in_1[15]);
  not not_5 (not_5_out, in_1[13]);
  not not_6 (not_6_out, in_1[14]);
  not not_7 (not_7_out, in_1[13]);
  not not_8 (not_8_out, in_1[12]);
  not not_9 (not_9_out, in_1[15]);
  not not_10 (not_10_out, in_1[12]);
  and and_1 (and_1_out, not_1_out, not_2_out, not_3_out);
  and and_2 (and_2_out, not_4_out, in_1[13], in_1[12]);
  and and_3 (and_3_out, in_1[14], not_5_out, in_1[12]);
  and and_4 (and_4_out, not_6_out, not_7_out, in_1[12]);
  and and_5 (and_5_out, in_1[15], not_8_out);
  and and_6 (and_6_out, in_1[15], in_1[13]);
  and and_7 (LoadStore, not_9_out, in_1[14], in_1[13], not_10_out);
  or or_1 (Rformat, and_1_out, and_2_out, and_3_out);
  or or_2 (Iformat, and_4_out, and_5_out, and_6_out);
endmodule

module jr (
  input  a,
  input  b,
  input  c,
  input  d,
  output jr
);

  wire not_1_out;

  not not_1 (not_1_out, c);
  and and_1 (jr, a, b, not_1_out, d);
endmodule
